// Logisim project lab.circ as structural Verilog: 2 circuits, main circuit main
module main (
  input  [1:0] act,
  input  [2:0] r1,
  input  [3:0] r2,
  input  [2:0] r3,
  input  [3:0] r4,
  input  [2:0] r5,
  input  [3:0] r6,
  input  [2:0] r7,
  output [1:0] out_9,
  output [1:0] out_10,
  output [1:0] out_11,
  output [3:0] out_12,
  output out_13,
  output out_14,
  output [2:0] out_15,
  output out_16,
  output [1:0] out_17
);

  wire active, and_1_out, and_2_out, bitselector_1_out, bitselector_2_out, bitselector_3_out,
       bitselector_4_out, bitselector_6_out, clk, d_ff_1_q, decoder_1_out0, decoder_1_out1, decoder_1_out2,
       decoder_1_out3, multiplexer_4_out, multiplexer_10_out, multiplexer_11_out, multiplexer_12_out,
       multiplexer_13_out, multiplexer_14_out, not_1_out, or_1_out, or_2_out, rst, start;
  wire [1:0] adder_1_out, adder_2_out, adder_3_out, adder_4_out, adder_5_out, adder_6_out, adder_7_out,
       adder_8_out, dir, multiplexer_1_out, multiplexer_2_out, multiplexer_5_out, multiplexer_6_out,
       multiplexer_7_out, multiplexer_8_out, multiplexer_9_out, multiplexer_21_out, register_3_q,
       register_4_q, subtractor_1_out, subtractor_2_out;
  wire [3:0] multiplexer_15_out, multiplexer_16_out, multiplexer_17_out, multiplexer_18_out;
  wire [8:0] field_1_out_8, field_1_out_9, field_1_out_10, field_1_out_11, field_1_out_12, field_1_out_13,
       field_1_out_14, field_1_out_15, field_1_out_16;

  Clock u_clk (.out(clk));
  Button u_rst (.out(rst));
  Button u_start (.out(start));
  LED led_1 (.in(active));
  Decoder #(.select(2), .disabled(0), .enable("false")) decoder_1 (
    .out0(decoder_1_out0), .out1(decoder_1_out1), .out2(decoder_1_out2), .out3(decoder_1_out3), .sel(dir));
  Adder #(.width(2)) adder_1 (.a(2'b01), .b(out_11), .out(adder_1_out));  // open: cin, cout
  Adder #(.width(2)) adder_2 (.a(2'b11), .b(out_11), .out(adder_2_out));  // open: cin, cout
  Adder #(.width(2)) adder_3 (.a(2'b10), .b(out_11), .out(adder_3_out));  // open: cin, cout
  Multiplexer #(.select(2), .width(2), .enable("false")) multiplexer_1 (
    .in0(2'b11), .in1(2'b10), .in2(2'b01), .in3(2'b00), .out(multiplexer_1_out), .sel(adder_4_out));
  Adder #(.width(2)) adder_4 (.a(out_10), .b(2'b01), .out(adder_4_out));  // open: cin, cout
  LED led_2 (.in(decoder_1_out0));
  LED led_3 (.in(decoder_1_out3));
  LED led_4 (.in(decoder_1_out2));
  LED led_5 (.in(decoder_1_out1));
  field field_1 (
    .in_1(r1), .in_2(r2), .in_3(r3), .in_4(r4), .in_5(r5), .in_6(r6), .in_7(r7), .out_8(field_1_out_8),
    .out_9(field_1_out_9), .out_10(field_1_out_10), .out_11(field_1_out_11), .out_12(field_1_out_12),
    .out_13(field_1_out_13), .out_14(field_1_out_14), .out_15(field_1_out_15), .out_16(field_1_out_16));
  DotMatrix #(.inputtype("row"), .matrixcols(9), .matrixrows(9)) dotmatrix_1 (
    .row0(field_1_out_8), .row1(field_1_out_9), .row2(field_1_out_10), .row3(field_1_out_11),
    .row4(field_1_out_12), .row5(field_1_out_13), .row6(field_1_out_14), .row7(field_1_out_15),
    .row8(field_1_out_16));
  Multiplexer #(.select(2), .width(2), .disabled(0), .enable("false")) multiplexer_2 (
    .in0(adder_1_out), .in1(adder_2_out), .in2(adder_3_out), .in3(out_11), .out(multiplexer_2_out), .sel(act));
  Adder #(.width(2)) adder_5 (.a(out_10), .b(2'b01), .out(adder_5_out));  // open: cin, cout
  Adder #(.width(2)) adder_6 (.a(out_10), .b(2'b11), .out(adder_6_out));  // open: cin, cout
  Adder #(.width(2)) adder_7 (.a(out_9), .b(2'b11), .out(adder_7_out));  // open: cin, cout
  Adder #(.width(2)) adder_8 (.a(out_9), .b(2'b01), .out(adder_8_out));  // open: cin, cout
  BitSelector #(.width(2)) bitselector_1 (.in(out_11), .out(bitselector_1_out), .sel(1'b1));
  not not_1 (not_1_out, bitselector_1_out);
  Multiplexer #(.select(2), .width(3), .enable("false")) multiplexer_3 (
    .in0(r1), .in1(r3), .in2(r5), .in3(r7), .out(out_15), .sel(out_9));
  Multiplexer #(.select(2), .enable("false")) multiplexer_4 (
    .in0(start), .in1(start), .in2(start), .in3(multiplexer_10_out), .out(multiplexer_4_out), .sel(act));
  and and_1 (and_1_out, multiplexer_4_out, active);
  Multiplexer #(.select(2), .width(2), .enable("false")) multiplexer_5 (
    .in0(out_10), .in1(adder_5_out), .in2(out_10), .in3(adder_6_out), .out(multiplexer_5_out), .sel(out_11));
  Multiplexer #(.select(2), .width(2), .enable("false")) multiplexer_6 (
    .in0(adder_7_out), .in1(out_9), .in2(adder_8_out), .in3(out_9), .out(multiplexer_6_out), .sel(out_11));
  BitSelector #(.width(3)) bitselector_2 (.in(out_15), .out(bitselector_2_out), .sel(multiplexer_1_out));
  BitSelector #(.width(3)) bitselector_3 (.in(out_15), .out(bitselector_3_out), .sel(multiplexer_7_out));
  Multiplexer #(.select(2), .width(2), .enable("false")) multiplexer_7 (
    .in0(2'b11), .in1(2'b10), .in2(2'b01), .in3(2'b00), .out(multiplexer_7_out), .sel(out_10));
  and and_2 (and_2_out, active, d_ff_1_q);
  or or_1 (or_1_out, and_2_out, start);
  D_Flip_Flop d_ff_1 (.clk(clk), .D(or_2_out), .Q(d_ff_1_q));  // open: Qn, preset, en, reset
  or or_2 (or_2_out, and_1_out, multiplexer_10_out, rst);
  Multiplexer #(.width(2), .enable("false")) multiplexer_8 (
    .in0(out_10), .in1(multiplexer_5_out), .out(multiplexer_8_out), .sel(multiplexer_10_out));
  Multiplexer #(.width(2), .enable("false")) multiplexer_9 (
    .in0(out_9), .in1(multiplexer_6_out), .out(multiplexer_9_out), .sel(multiplexer_10_out));
  Multiplexer #(.select(2), .enable("false")) multiplexer_10 (
    .in0(1'b0), .in1(1'b0), .in2(1'b0), .in3(out_14), .out(multiplexer_10_out), .sel(act));
  BitSelector #(.width(2)) bitselector_4 (.in(out_11), .out(bitselector_4_out), .sel(1'b1));
  Multiplexer #(.enable("false")) multiplexer_11 (
    .in0(1'b0), .in1(bitselector_2_out), .out(multiplexer_11_out), .sel(not_1_out));
  Multiplexer #(.enable("false")) multiplexer_12 (
    .in0(bitselector_3_out), .in1(bitselector_2_out), .out(multiplexer_12_out), .sel(not_1_out));
  Multiplexer #(.enable("false")) multiplexer_13 (
    .in0(bitselector_3_out), .in1(bitselector_2_out), .out(multiplexer_13_out), .sel(not_1_out));
  Multiplexer #(.enable("false")) multiplexer_14 (
    .in0(bitselector_3_out), .in1(1'b0), .out(multiplexer_14_out), .sel(not_1_out));
  Register #(.width(1)) register_1 (.D(or_1_out), .Q(active), .clk(clk), .clr(rst));  // open: en
  Register #(.width(2)) register_2 (.D(multiplexer_2_out), .en(active), .Q(out_11), .clk(clk), .clr(rst));
  Subtractor #(.width(2)) subtractor_1 (.a(multiplexer_8_out), .b(2'b11), .out(subtractor_1_out));  // open: bin, bout
  Subtractor #(.width(2)) subtractor_2 (.a(multiplexer_9_out), .b(2'b11), .out(subtractor_2_out));  // open: bin, bout
  Multiplexer #(.width(4), .enable("false")) multiplexer_15 (
    .in0(4'b0000), .in1(r2), .out(multiplexer_15_out), .sel(bitselector_4_out));
  Multiplexer #(.width(4), .enable("false")) multiplexer_16 (
    .in0(r2), .in1(r4), .out(multiplexer_16_out), .sel(bitselector_4_out));
  Multiplexer #(.width(4), .enable("false")) multiplexer_17 (
    .in0(r4), .in1(r6), .out(multiplexer_17_out), .sel(bitselector_4_out));
  Multiplexer #(.width(4), .enable("false")) multiplexer_18 (
    .in0(r6), .in1(4'b0000), .out(multiplexer_18_out), .sel(bitselector_4_out));
  Register #(.width(2)) register_3 (.D(subtractor_1_out), .en(active), .Q(register_3_q), .clk(clk), .clr(rst));
  Register #(.width(2)) register_4 (.D(subtractor_2_out), .en(active), .Q(register_4_q), .clk(clk), .clr(rst));
  Multiplexer #(.select(2), .width(4), .enable("false")) multiplexer_19 (
    .in0(multiplexer_15_out), .in1(multiplexer_16_out), .in2(multiplexer_17_out), .in3(multiplexer_18_out),
    .out(out_12), .sel(out_9));
  Multiplexer #(.select(2), .enable("false")) multiplexer_20 (
    .in0(multiplexer_11_out), .in1(multiplexer_12_out), .in2(multiplexer_13_out), .in3(multiplexer_14_out),
    .out(out_16), .sel(out_10));
  Adder #(.width(2)) adder_9 (.a(register_3_q), .b(2'b11), .out(out_10));  // open: cin, cout
  Adder #(.width(2)) adder_10 (.a(register_4_q), .b(2'b11), .out(out_9));  // open: cin, cout
  BitSelector #(.width(4)) bitselector_5 (.in(out_12), .out(out_13), .sel(multiplexer_21_out));
  Multiplexer #(.select(2), .width(2), .enable("false")) multiplexer_21 (
    .in0(2'b11), .in1(2'b10), .in2(2'b01), .in3(2'b00), .out(multiplexer_21_out), .sel(out_10));
  Multiplexer #(.select(2), .width(2), .enable("false")) multiplexer_22 (
    .in0(2'b00), .in1(2'b10), .in2(2'b01), .in3(2'b11), .out(dir), .sel(out_11));
  BitSelector #(.width(2)) bitselector_6 (.in(out_11), .out(bitselector_6_out), .sel(1'b0));
  Multiplexer #(.enable("false")) multiplexer_23 (.in0(out_13), .in1(out_16), .out(out_14), .sel(bitselector_6_out));

  assign out_17 = out_10;

  // Other names for the same wires on the sheet: col[1:0] = out_10; row[1:0] = out_9; xrow[1:0] = act
endmodule

module field (
  input  [2:0] in_1,
  input  [3:0] in_2,
  input  [2:0] in_3,
  input  [3:0] in_4,
  input  [2:0] in_5,
  input  [3:0] in_6,
  input  [2:0] in_7,
  output [8:0] out_8,
  output [8:0] out_9,
  output [8:0] out_10,
  output [8:0] out_11,
  output [8:0] out_12,
  output [8:0] out_13,
  output [8:0] out_14,
  output [8:0] out_15,
  output [8:0] out_16
);


  assign out_8 = {9{1'b0}};
  assign out_9 = {2'b01, in_1[2], 1'b1, in_1[1], 1'b1, in_1[0], 2'b10};
  assign out_10 = {1'b0, in_2[3], 1'b0, in_2[2], 1'b0, in_2[1], 1'b0, in_2[0], 1'b0};
  assign out_11 = {2'b01, in_3[2], 1'b1, in_3[1], 1'b1, in_3[0], 2'b10};
  assign out_12 = {1'b0, in_4[3], 1'b0, in_4[2], 1'b0, in_4[1], 1'b0, in_4[0], 1'b0};
  assign out_13 = {2'b01, in_5[2], 1'b1, in_5[1], 1'b1, in_5[0], 2'b10};
  assign out_14 = {1'b0, in_6[3], 1'b0, in_6[2], 1'b0, in_6[1], 1'b0, in_6[0], 1'b0};
  assign out_15 = {2'b01, in_7[2], 1'b1, in_7[1], 1'b1, in_7[0], 2'b10};
  assign out_16 = {9{1'b0}};
endmodule
